// Logisim project Submit.circ as structural Verilog: 3 circuits, main circuit Black Box Test
module Black_Box_Test (
  input  b3,
  input  b2,
  input  b1,
  input  b0,
  input  a3,
  input  a2,
  input  a1,
  input  a0,
  input  d0,
  input  d1,
  output c_out,
  output s3,
  output s2,
  output s1,
  output s0
);

  ALU alu_1 (
    .d0(d0), .d1(d1), .c_out(c_out), .b3(b3), .b2(b2), .b1(b1), .b0(b0), .a3(a3), .a2(a2), .a1(a1), .a0(a0),
    .s3(s3), .s2(s2), .s1(s1), .s0(s0));  // open: in_10, in_11, in_12, in_13

  // Notes on the sheet:
  //   ALU Control d1 d0
  //   00 = add 
  //   01 = sub
  //   10 = dec 
  //   11 = inc 
  //   Black Box Testing of 4-bit ALU
endmodule

// 4-bit ALU
module ALU (
  input  b3,
  input  b2,
  input  b1,
  input  b0,
  input  a3,
  input  a2,
  input  a1,
  input  a0,
  input  d0,
  input  in_10,
  input  in_11,
  input  in_12,
  input  in_13,
  input  d1,
  output c_out,
  output s3,
  output s2,
  output s1,
  output s0
);

  wire full_adder_2_cout, full_adder_3_cout, full_adder_4_cout, undriven;

  Full_Adder full_adder_1 (.cin(full_adder_2_cout), .x(a3), .y(b0), .Sum(s3), .cout(c_out));
  NotExactlyOne xnor_1 (.out(b0), .in0(b0), .in1(b0), .in2(b0), .in3(b0));
  NotExactlyOne xnor_2 (.out(b0), .in1(b0), .in2(b0), .in3(b0));
  Full_Adder full_adder_2 (.cin(full_adder_3_cout), .x(a2), .y(b0), .Sum(s2), .cout(full_adder_2_cout));
  Full_Adder full_adder_3 (.cin(full_adder_4_cout), .x(a1), .y(b1), .Sum(s1), .cout(full_adder_3_cout));
  xnor xnor_3 (b1, b1, b0);
  xnor xnor_4 (b0, b0, b0);
  Full_Adder full_adder_4 (.cin(undriven), .x(a0), .y(b0), .Sum(s0), .cout(full_adder_4_cout));

  assign b2 = b0;
  assign b3 = b0;
  assign d1 = b0;
  assign in_10 = a2;
  assign in_11 = a1;
  assign in_12 = a0;

  // Notes on the sheet:
  //   c_in
  //   x3
  //   x2
  //   x1
  //   x0
endmodule

// FA
module Full_Adder (
  input  cin,
  input  x,
  input  y,
  output Sum,
  output cout
);

  wire and_1_out, and_2_out, xor_1_out;

  and and_1 (and_1_out, x, y);
  xor xor_1 (xor_1_out, x, y);
  and and_2 (and_2_out, cin, xor_1_out);
  xor xor_2 (Sum, cin, xor_1_out);
  or or_1 (cout, and_2_out, and_1_out);

  // Notes on the sheet:
  //   Full Adder
endmodule
